# Fritzing sketch LEDStrip (saved by Fritzing 0.9.4)
breadboards: 2

parts:
  12V_Input1 = Power plug
  R2 = Resistor [tolerance=±1% resistance=1k package=THT]
  R3 = Resistor [tolerance=±5% resistance=220 package=THT]
  C1 = Electrolytic Capacitor [capacitance=220µF voltage=20V package="100 mil [THT, electrolytic]"]
  R4 = Resistor [tolerance=±1% resistance=200k package=THT]
  R5 = Resistor [tolerance=±1% resistance=100k package=THT]  # not connected
  R6 = Resistor [tolerance=±1% resistance=2k package=THT]
  R7 = Resistor [tolerance=±1% resistance=15k package=THT]  # not connected
  R8 = Resistor [tolerance=±1% resistance=47k package=THT]  # not connected
  R10 = Resistor [tolerance=±1% resistance=330 package=THT]
  R9 = Resistor [tolerance=±1% resistance=9.1k package=THT]  # not connected
  50K = POT [package=3362u]  # not connected
  C2 = Electrolytic Capacitor [capacitance=470µF voltage=20V package="100 mil [THT, electrolytic]"]
  M1 = ESP32-S2-DevKitC-1 [part_number=ESP32-S2-DevKitC-1]
  LED_Strip_Addressable = female pin header, 3 pins [form="♀ (female)"]
  Part2 = LED Tactile Button Breakout v10 [part_number=BOB-10467]  # not connected
  LCD = female pin header, 4 pins [form="♀ (female)"]
  LCD1 = female pin header, 4 pins [form="♀ (female)"]  # not connected
  Step_Down_Power1 = longpad pin header, 4 pins [form="long pad"]  # not connected
  5v = female pin header, 2 pins [form="♀ (female)"]
  3_3v = female pin header, 2 pins [form="♀ (female)"]
  12v = female pin header, 2 pins [form="♀ (female)"]
  U1 = Voltage Regulator - 5V [package="DPak [SMD]"]  # not connected
  U4 = SPX29302 [package=q5-dd_spx29300]  # not connected
  D1 = Rectifier Diode [part_number=1N4001 package="300 mil [THT]"]  # not connected
  D4 = Diode [package=smb-diode]  # not connected
  D2 = Rectifier Diode [package="Melf DO-213 AA [SMD]"]  # not connected
  D6 = Rectifier Diode [package="Melf DO-213 AA [SMD]"]  # not connected
  D5 = Diode [package=sma-diode]  # not connected
  D3 = Rectifier Diode [package="Melf DO-213 AA [SMD]"]
  L1 = Inductor [package="1206 [SMD]"]  # not connected
  33uH = Inductors [package=cr54]
  C3 = Electrolytic Capacitor [capacitance=220µF voltage=20V package="100 mil [THT, electrolytic]"]
  mic1 = female pin header, 5 pins [form="♀ (female)"]
  D8 = Rectifier Diode [package="Melf DO-213 AA [SMD]"]
  C7 = Electrolytic Capacitor [capacitance=1µF package="100 mil [THT, electrolytic]"]
  C8 = Electrolytic Capacitor [capacitance=1µF package="100 mil [THT, electrolytic]"]
  C9 = Electrolytic Capacitor [capacitance=1µF package="100 mil [THT, electrolytic]"]
  33uH_2 = Inductors [package=cr54]
  5v1 = female pin header, 2 pins [form="♀ (female)"]
  3_3v1 = female pin header, 2 pins [form="♀ (female)"]
  12v1 = female pin header, 2 pins [form="♀ (female)"]
  MSGEQ1 = MSGEQ7 [chip_label=IC package="DIP (Dual Inline) [THT]"]
  LM2596_1 = LM2596 [package=q5-dd_spx29300]
  LM2596_2 = LM2596 [package=q5-dd_spx29300]
  33pF = Capacitor [package=0603-cap]
  100nF = Capacitor [package=0603-cap]
  C11 = Tantalum Capacitor [capacitance=1µF package="A 3216 [SMD, tantalum]"]  # not connected
  10nF = Capacitor [package=0603-cap]
  100nF_2 = Capacitor [package=0603-cap]
  R11 = Resistor [tolerance=±1% resistance=20k package=THT]
  SJ3 = Solder Jumper [package=sj_3_paste1_2]
  MOSFET11 = MOSFET-NCHANNEL [package=sot23-3]
  MOSFET12 = MOSFET-NCHANNEL [package=sot23-3]
  MOSFET13 = MOSFET-NCHANNEL [package=sot23-3]
  LED_Strip1 = female pin header, 4 pins [form="♀ (female)"]
  LED_Matrix1 = female pin header, 5 pins [form="♀ (female)"]

nets:
  GND: 12V_Input1.GND, R2.Pin_1, R3.Pin_0, C1.-, C2.-, M1.pin_22, M1.pin_23, M1.pin_24, M1.pin_44, LED_Strip_Addressable.pin3, 5v.pin1, 3_3v.pin1, 12v.pin1, D3.anode, C3.-, mic1.pin5, D8.anode, C7.-, C8.-, C9.-, 5v1.pin1, 12v1.pin1, LM2596_1.GND, LM2596_1.On/Off, LM2596_2.GND, LM2596_2.On/Off, 33pF.2, 100nF.1, SJ3.1
  VIN: 12V_Input1.VCC, C1.+, C2.+, 12v.pin2, C7.+, C9.+, 12v1.pin2, LM2596_1.VIN, LM2596_2.VIN, LED_Strip1.pin4
  N1: R2.Pin_0, M1.pin_4
  N2: R4.Pin_0, M1.pin_21, 33uH.2, C3.+, MSGEQ1.VDD, LM2596_1.Feedback, 100nF_2.2, SJ3.3
  N3: R4.Pin_1, MSGEQ1.CKIN, 33pF.1
  N4: R6.Pin_0, 10nF.2
  N5: R6.Pin_1, R11.Pin_0
  N6: R10.Pin_0, M1.pin_39
  N7: R10.Pin_1, LED_Strip_Addressable.pin2
  N8: M1.pin_1, M1.pin_2, LCD.pin1, 5v.pin2, mic1.pin4, 5v1.pin2
  N9: M1.pin_5, MSGEQ1.GND
  N10: M1.pin_11, LCD.pin3
  N11: M1.pin_15, LCD.pin2
  N12: M1.pin_29, LED_Matrix1.pin2
  N13: M1.pin_30, LED_Matrix1.pin1
  N14: M1.pin_31, LED_Matrix1.pin3
  N15: M1.pin_36, MOSFET11.G
  N16: M1.pin_37, MOSFET12.G
  N17: M1.pin_38, MOSFET13.G
  N18: M1.pin_40, MSGEQ1.STROBE
  N19: M1.pin_41, MSGEQ1.OUT
  N20: LED_Strip_Addressable.pin1, 3_3v.pin2
  N21: D3.cathode, 33uH.1, LM2596_1.OUT
  N22: mic1.pin2, R11.Pin_1
  N23: mic1.pin3, SJ3.2
  N24: D8.cathode, 33uH_2.1, LM2596_2.OUT
  N25: C8.+, 33uH_2.2, 3_3v1.pin2, LM2596_2.Feedback, LED_Matrix1.pin5
  N26: 3_3v1.pin1, MSGEQ1.VSS, 100nF_2.1, MOSFET11.S, MOSFET12.S, MOSFET13.S, MOSFET13.D, LED_Strip1.pin3, LED_Matrix1.pin4
  N27: MSGEQ1.IN, 10nF.1
  N28: MSGEQ1.pin6, 100nF.2
  N29: MOSFET11.D, LED_Strip1.pin1
  N30: MOSFET12.D, LED_Strip1.pin2

notes:
  B R G P
  Note that the ESP32 board below is ESP32 S2. I'm actually using ESP32 S3 so I'm keeping the pin LOCATION constant and ignoring the pin NUMBERS for the bottom rail which differ between S2 and S3.

custom parts:
  ESP32-S2-DevKitC-1: ESP32-S2-DevKitC-1 is an entry-level development board based on ESP32-S2-SOLO (on-board PCB antenna). It is based on the ESP32 microcontroller that boasts Wifi, Bluetooth, Ethernet and Low Power support all in a single chip. (vanepp) Feb 2022: converted to ESP32-S2-DevKitC-1. This module is 44pins long (2x22) and 11 pins width.
  MSGEQ7: A DIP stand-in part for whatever IC you want. With 8 pins on a 300mil dual inline package (DIP) footprint.
  LM2596: LM2596 SIMPLE SWITCHER® Power Converter 150-kHz 3-A Step-Down Voltage Regulator
